# Fritzing sketch prototype_rp2040_via_2x4 (saved by Fritzing 0.9.6b)
breadboards: 1

parts:
  Mod1 = Raspberry Pi Pico
  S2 = Pushbutton [package="[THT]"]
  S3 = Pushbutton [package="[THT]"]
  S4 = Pushbutton [package="[THT]"]
  S5 = Pushbutton [package="[THT]"]
  S6 = Pushbutton [package="[THT]"]
  S7 = Pushbutton [package="[THT]"]
  S8 = Pushbutton [package="[THT]"]
  S1 = Pushbutton [package="[THT]"]

nets:
  N1: Mod1.pin_3, Mod1.pin_8, Mod1.pin_13, Mod1.pin_18, Mod1.pin_23, Mod1.pin_28, Mod1.pin_33, Mod1.pin_38, Mod1.pin_42, S2.Pin_1, S2.Pin_2, S3.Pin_1, S3.Pin_2, S4.Pin_1, S4.Pin_2, S5.Pin_1, S5.Pin_2, S6.Pin_1, S6.Pin_2, S7.Pin_1, S7.Pin_2, S8.Pin_1, S8.Pin_2, S1.Pin_1, S1.Pin_2
  N2: Mod1.pin_9, S8.Pin_3, S8.Pin_4
  N3: Mod1.pin_10, S7.Pin_3, S7.Pin_4
  N4: Mod1.pin_11, S6.Pin_3, S6.Pin_4
  N5: Mod1.pin_12, S5.Pin_3, S5.Pin_4
  N6: Mod1.pin_14, S4.Pin_3, S4.Pin_4
  N7: Mod1.pin_15, S3.Pin_3, S3.Pin_4
  N8: Mod1.pin_16, S2.Pin_3, S2.Pin_4
  N9: Mod1.pin_17, S1.Pin_3, S1.Pin_4

custom parts:
  Raspberry Pi Pico: Raspberry Pi Pico. Based around the RP2040 microcontroller the Pico is a low cost microcontroller device bringing Raspberry Pi quality, cost, and easy of use to the microcontroller space. Jan 2021, Split part in to two versions: tht (this one) and SMD. This one will drill holes for a .1 in header in pcb to allow plugging in the module as well as providing pads to solder the module to the top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
